// Logisim project guia02.circ as structural Verilog: 10 circuits, main circuit E06
module E06 (
  input  A,
  input  B,
  input  C,
  output s
);

  wire and_1_out, and_2_out, not_1_out;

  not not_1 (not_1_out, B);
  and and_1 (and_1_out, not_1_out, A);
  and and_2 (and_2_out, C, B);
  or or_1 (s, and_1_out, and_2_out);
endmodule

module dmux_1_4_E07 (
  input  c0,
  input  c1,
  input  e,
  output s0,
  output s1,
  output s2,
  output s3
);

  wire and_2_out, and_4_out, and_6_out, and_8_out, not_1_out, not_2_out, not_3_out, not_4_out;

  not not_1 (not_1_out, c0);
  not not_2 (not_2_out, c1);
  not not_3 (not_3_out, c1);
  not not_4 (not_4_out, c0);
  and and_1 (s0, e, and_2_out);
  and and_2 (and_2_out, not_1_out, not_2_out);
  and and_3 (s1, e, and_4_out);
  and and_4 (and_4_out, c0, not_3_out);
  and and_5 (s2, e, and_6_out);
  and and_6 (and_6_out, not_4_out, c1);
  and and_7 (s3, e, and_8_out);
  and and_8 (and_8_out, c0, c1);
endmodule

module encoder_4_2_E08 (
  input  e0,
  input  e1,
  input  e2,
  input  e3,
  output s0,
  output s1,
  output I
);

  wire and_1_out, and_2_out, and_3_out, and_4_out, and_5_out, and_6_out, and_7_out, and_8_out, and_9_out,
       not_1_out, not_2_out, not_3_out, not_4_out, not_5_out, not_6_out, not_7_out, not_8_out, not_9_out,
       or_3_out, or_4_out, or_5_out;

  or or_1 (s0, e1, e3);
  or or_2 (s1, e3, e2);
  not not_1 (not_1_out, e1);
  not not_2 (not_2_out, e0);
  not not_3 (not_3_out, e2);
  not not_4 (not_4_out, e1);
  not not_5 (not_5_out, e3);
  not not_6 (not_6_out, e2);
  and and_1 (and_1_out, e0, not_1_out);
  and and_2 (and_2_out, and_1_out, not_7_out);
  not not_7 (not_7_out, e2);
  not not_8 (not_8_out, e3);
  and and_3 (and_3_out, e1, not_3_out);
  and and_4 (and_4_out, and_3_out, not_9_out);
  not not_9 (not_9_out, e3);
  and and_5 (and_5_out, e2, not_5_out);
  and and_6 (and_6_out, not_6_out, e3);
  and and_7 (and_7_out, and_2_out, not_8_out);
  and and_8 (and_8_out, not_4_out, or_3_out);
  or or_3 (or_3_out, and_5_out, and_6_out);
  or or_4 (or_4_out, and_4_out, and_8_out);
  and and_9 (and_9_out, not_2_out, or_4_out);
  or or_5 (or_5_out, and_7_out, and_9_out);
  not not_10 (I, or_5_out);
endmodule

module decoder_2_4_E09A (
  input  e0,
  input  e1,
  output s0,
  output s1,
  output s2,
  output s3
);

  wire not_1_out, not_2_out, not_3_out, not_4_out;

  not not_1 (not_1_out, e0);
  not not_2 (not_2_out, e1);
  not not_3 (not_3_out, e1);
  not not_4 (not_4_out, e0);
  and and_1 (s0, not_1_out, not_2_out);
  and and_2 (s1, e0, not_3_out);
  and and_3 (s2, not_4_out, e1);
  and and_4 (s3, e0, e1);
endmodule

module dmux_1_4_E09B (
  input  c0,
  input  c1,
  input  e,
  output s0,
  output s1,
  output s2,
  output s3
);

  wire decoder_2_4_e09a_1_s0, decoder_2_4_e09a_1_s1, decoder_2_4_e09a_1_s2, decoder_2_4_e09a_1_s3;

  decoder_2_4_E09A decoder_2_4_e09a_1 (
    .e0(c0), .e1(c1), .s0(decoder_2_4_e09a_1_s0), .s1(decoder_2_4_e09a_1_s1), .s2(decoder_2_4_e09a_1_s2),
    .s3(decoder_2_4_e09a_1_s3));
  and and_1 (s0, decoder_2_4_e09a_1_s0, e);
  and and_2 (s1, decoder_2_4_e09a_1_s1, e);
  and and_3 (s2, decoder_2_4_e09a_1_s2, e);
  and and_4 (s3, decoder_2_4_e09a_1_s3, e);
endmodule

module carry_left_shifter_3_4_E10 (
  input  e0,
  input  e1,
  input  e2,
  input  c,
  output s0,
  output s1,
  output s2,
  output s3
);

  wire and_2_out, and_3_out, and_4_out, and_5_out, not_1_out, not_2_out, not_3_out;

  not not_1 (not_1_out, c);
  not not_2 (not_2_out, c);
  not not_3 (not_3_out, c);
  and and_1 (s0, not_1_out, e0);
  and and_2 (and_2_out, not_2_out, e1);
  and and_3 (and_3_out, c, e0);
  and and_4 (and_4_out, not_3_out, e2);
  and and_5 (and_5_out, c, e1);
  and and_6 (s3, c, e2);
  or or_1 (s1, and_2_out, and_3_out);
  or or_2 (s2, and_4_out, and_5_out);
endmodule

module reg_4_E16 (
  input  i0,
  input  i1,
  input  i2,
  input  i3,
  input  load,
  output o0,
  output o1,
  output o2,
  output o3
);

  wire clock_1_out, multiplexer_1_out, multiplexer_2_out, multiplexer_3_out, multiplexer_4_out;

  D_Flip_Flop d_ff_1 (.D(multiplexer_1_out), .clk(clock_1_out), .Q(o0));  // open: Qn, preset, reset
  Multiplexer multiplexer_1 (.in0(o0), .in1(i0), .out(multiplexer_1_out), .sel(load));
  D_Flip_Flop d_ff_2 (.D(multiplexer_2_out), .clk(clock_1_out), .Q(o1));  // open: Qn, preset, reset
  Multiplexer multiplexer_2 (.in0(o1), .in1(i1), .out(multiplexer_2_out), .sel(load));
  D_Flip_Flop d_ff_3 (.D(multiplexer_3_out), .clk(clock_1_out), .Q(o2));  // open: Qn, preset, reset
  Multiplexer multiplexer_3 (.in0(o2), .in1(i2), .out(multiplexer_3_out), .sel(load));
  D_Flip_Flop d_ff_4 (.D(multiplexer_4_out), .clk(clock_1_out), .Q(o3));  // open: Qn, preset, reset
  Multiplexer multiplexer_4 (.in0(o3), .in1(i3), .out(multiplexer_4_out), .sel(load));
  Clock clock_1 (.out(clock_1_out));
endmodule

module reg_extensor_de_signo_4_E17 (
  input  i0,
  input  i1,
  input  i2,
  input  i3,
  input  load,
  input  ext,
  output o0,
  output o1,
  output o2,
  output o3
);

  wire [3:0] reg_4_e16_1_o2;

  reg_4_E16 reg_4_e16_1 (
    .i0(i0), .i1(i1), .i2(i2), .i3(i3), .load(load), .o0(reg_4_e16_1_o2[0]), .o1(reg_4_e16_1_o2[1]),
    .o2(reg_4_e16_1_o2[2]), .o3(reg_4_e16_1_o2[3]));
  Multiplexer #(.width(4)) multiplexer_1 (
    .in0(reg_4_e16_1_o2), .in1({{2{reg_4_e16_1_o2[3]}}, reg_4_e16_1_o2[1:0]}), .out({o3, o2, o1, o0}),
    .sel(ext));
endmodule

module reg_salida_restringida_4_E18 (
  input  i0,
  input  i1,
  input  i2,
  input  i3,
  input  load,
  input  read,
  output o0,
  output o1,
  output o2,
  output o3
);

  wire clock_1_out, d_ff_1_q;
  wire [3:0] reg_4_e16_1_o0;

  D_Flip_Flop d_ff_1 (.D(read), .clk(clock_1_out), .Q(d_ff_1_q));  // open: Qn, preset, reset
  Clock clock_1 (.out(clock_1_out));
  reg_4_E16 reg_4_e16_1 (
    .i0(i0), .i1(i1), .i2(i2), .i3(i3), .load(load), .o0(reg_4_e16_1_o0[0]), .o1(reg_4_e16_1_o0[1]),
    .o2(reg_4_e16_1_o0[2]), .o3(reg_4_e16_1_o0[3]));
  assign {o3, o2, o1, o0} = d_ff_1_q ? reg_4_e16_1_o0 : 4'bz;  // Controlled_Buffer controlled_buffer_1
endmodule

module ALU_reg_4_E20 (
  input  B3,
  input  B2,
  input  B1,
  input  B0,
  input  A3,
  input  A2,
  input  A1,
  input  A0,
  input  load_B,
  input  load_A,
  input  add,
  input  sub,
  input  and_log,
  input  or_log,
  input  read_out,
  output V,
  output C,
  output N,
  output Z,
  output o0,
  output o1,
  output o2,
  output o3
);

  wire [1:0] encoder_4_2_e08_1_s0;
  wire [3:0] alu_4_1_s, reg_4_e16_1_o0, reg_4_e16_2_o0;

  reg_4_E16 reg_4_e16_1 (
    .i0(B0), .i1(B1), .i2(B2), .i3(B3), .load(load_B), .o0(reg_4_e16_1_o0[0]), .o1(reg_4_e16_1_o0[1]),
    .o2(reg_4_e16_1_o0[2]), .o3(reg_4_e16_1_o0[3]));
  reg_4_E16 reg_4_e16_2 (
    .i0(A0), .i1(A1), .i2(A2), .i3(A3), .load(load_A), .o0(reg_4_e16_2_o0[0]), .o1(reg_4_e16_2_o0[1]),
    .o2(reg_4_e16_2_o0[2]), .o3(reg_4_e16_2_o0[3]));
  encoder_4_2_E08 encoder_4_2_e08_1 (
    .e0(add), .e1(sub), .e2(and_log), .e3(or_log), .s0(encoder_4_2_e08_1_s0[0]), .s1(encoder_4_2_e08_1_s0[1]));  // open: I
  ALU_4 alu_4_1 (
    .A(reg_4_e16_2_o0), .B(reg_4_e16_1_o0), .OP(encoder_4_2_e08_1_s0), .V(V), .C(C), .S(alu_4_1_s), .N(N),
    .Z(Z));
  reg_salida_restringida_4_E18 reg_salida_restringida_4_e18_1 (
    .i0(alu_4_1_s[0]), .i1(alu_4_1_s[1]), .i2(alu_4_1_s[2]), .i3(alu_4_1_s[3]), .load(1'b1), .read(read_out),
    .o0(o0), .o1(o1), .o2(o2), .o3(o3));
endmodule
